# Fritzing sketch 회로도 (saved by Fritzing 0.9.9b)
breadboards: 1

parts:
  J1 = Basic Force Sensing Resistor (FSR) [package=THT]
  J2 = Basic Force Sensing Resistor (FSR) [package=THT]
  J3 = Basic Force Sensing Resistor (FSR) [package=THT]
  R1 = Resistor [tolerance=±5% power=0.25 resistance=330 package=THT]
  R2 = Resistor [tolerance=±5% power=0.25 resistance=330 package=THT]
  R3 = Resistor [tolerance=±5% power=0.25 resistance=330 package=THT]
  LED1 = smd LED [color="Red (633nm)" package="0603 [SMD]"]
  LED2 = smd LED [color="Red (633nm)" package="0603 [SMD]"]
  LED3 = smd LED [color="Red (633nm)" package="0603 [SMD]"]
  LED4 = smd LED [color="Red (633nm)" package="0603 [SMD]"]
  LED5 = smd LED [color="Red (633nm)" package="0603 [SMD]"]
  R4 = Resistor [tolerance=±5% power=0.25 resistance=330 package=THT]
  R5 = Resistor [tolerance=±5% power=0.25 resistance=330 package=THT]
  R6 = Resistor [tolerance=±5% power=0.25 resistance=330 package=THT]
  R7 = Resistor [tolerance=±5% power=0.25 resistance=330 package=THT]
  R8 = Resistor [tolerance=±5% power=0.25 resistance=330 package=THT]
  부품1 = InvenSense MPU6050
  GY-NEO6MV1 = GY-NEO6MV2
  U1 = SUP500F [package=sup500f]  # not connected
  J4 = Piezo Speaker
  J5 = Piezo Speaker
  J7 = Piezo Speaker
  J8 = Piezo Speaker
  Adafruit_bq25185_with_5V_Boost_Breakout1 = Adafruit bq25185 with 5V Boost Breakout [part_number=#6106]
  M1 = advancer muscle sensor v3
  U2 = LIPO-110mAh [package=lipo-110]
  D1 = Diode [package=diode-1n4148]  # not connected
  D2 = Diode [package=diode-1n4148]
  D3 = Diode [package=diode-1n4148]
  D4 = Diode [package=diode-1n4148]
  D5 = Diode [package=diode-1n4148]
  D6 = Diode [package=diode-1n4148]
  D7 = Diode [package=diode-1n4148]
  D8 = Diode [package=diode-1n4148]
  D9 = Diode [package=diode-1n4148]
  D10 = Diode [package=diode-1n4148]
  D11 = Diode [package=diode-1n4148]
  D12 = Diode [package=diode-1n4148]
  D13 = Diode [package=diode-1n4148]
  D14 = Diode [package=diode-1n4148]
  D15 = Diode [package=diode-1n4148]
  D16 = Diode [package=diode-1n4148]
  C1 = Capacitor Polarized [package=cpol-radial-10uf-25v]
  C2 = Electrolytic Capacitor [capacitance=100µF voltage=35V package="200 mil [THT, electrolytic]"]
  U3 = Sharp Dust Sensor [part_number=GP2Y1010AU0F]
  부품4 = Arduino Mega ADK (Rev3)

nets:
  N1: J1.pin_0, R1.Pin_1, 부품4.A0
  GND: J1.pin_1, J2.pin_1, J3.pin_1, LED1.cathode, LED2.cathode, LED3.cathode, LED4.cathode, LED5.cathode, 부품1.GND, GY-NEO6MV1.GND, J4.pin1, J5.pin1, J7.pin1, J8.pin1, M1.GND, D4.C, D8.C, D12.C, D16.C, U3.S-GND, U3.Vo, 부품4.GND
  N2: J2.pin_0, 부품4.A1
  N3: J3.pin_0, R3.Pin_1, 부품4.A2
  VCC: R1.Pin_0, R2.Pin_0, R3.Pin_0, 부품1.VCC, GY-NEO6MV1.Vcc, J4.pin2, J5.pin2, J7.pin2, J8.pin2, M1.+Vs, D5.C, D9.C, D13.C, U3.VCC, 부품4.5V
  N4: LED1.anode, R4.Pin_1
  N5: LED2.anode, R6.Pin_1
  N6: LED3.anode, R8.Pin_1
  N7: LED4.anode, R7.Pin_1
  N8: LED5.anode, R5.Pin_1
  N9: R4.Pin_0, 부품4.D10_PWM
  N10: R5.Pin_0, 부품4.D9_PWM
  N11: R6.Pin_0, 부품4.D11_PWM
  N12: R7.Pin_0, 부품4.D8_PWM
  N13: R8.Pin_0, 부품4.D12_PWM
  N14: 부품1.SCL, 부품4.D21/SCL
  N15: 부품1.SDA, 부품4.D20/SDA
  N16: GY-NEO6MV1.Rx, 부품4.D19/RX1
  N17: GY-NEO6MV1.Tx, 부품4.D18/TX1
  N18: Adafruit_bq25185_with_5V_Boost_Breakout1.GND, U2.-, D3.C, D6.C, D10.C, D14.C
  N19: Adafruit_bq25185_with_5V_Boost_Breakout1.VBAT, U2.+, C1.-
  N20: M1.SIG, 부품4.A5
  N21: D2.C, D7.C, D11.C, D15.C, C1.+
  N22: C2.-, U3.LED-GND
  N23: C2.+, U3.V-LED
  N24: U3.LED, 부품4.D7_PWM

custom parts:
  GY-NEO6MV2: Description: Module GPS , type GY-NEO6MV2, pour arduino et autres micro-contrôleurs. Caractéristiques De type GY-NEO6MV2 Alimentation 3V-5V Avec Flight Control EEPROM MWC Antenne large céramique, fort signal, 25 x 25 mm Paramètres de configuration sauvegardés en EEPROM Avec batterie de backup de données LED témoin de signal Module miniaturisé 25 x 35 mm Trou de fixation de 3mm Baud rate par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
  Adafruit bq25185 with 5V Boost Breakout: We're always on the look out for better ways to make projects portable: being able to charge your battery in the most convenient manner will let projects run no matter what power is available. Then we added a power supply chip with it to let you run your project without a separate board. The result is the Adafruit bq25185 USB / DC / Solar Charger with 5V Boost Board! It uses the new bq25185 is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
  advancer muscle sensor v3: This sensor will measure the filtered and rectified electrical activity of a muscle; outputting 0-Vs Volts depending the amount of activity in the selected muscle, where Vs signifies the voltage of the power source. Power supply voltage: min. +-3.5V.
  Sharp Dust Sensor: Sharp GP2Y1010AU0F Dust Sensor
